# Fritzing sketch blinker (saved by Fritzing 0.8.7b)
circuit board: 3cm x 2.7cm
breadboards: 1

parts:
  J1 = Screw terminal - 2 pins [package=THT]
  1 = 555 Timer [package="SO8 [SMD]"]
  LED1 = smd LED [color="Red (633nm)" package="1206 [SMD]"]
  R3 = Resistor [tolerance=±5% resistance=1.5k package="1206 [SMD]"]
  C1 = Tantalum Capacitor [capacitance=10µF package="C 6032 [SMD, tantalum]"]
  R1 = Resistor [tolerance=±5% resistance=68k package="1206 [SMD]"]
  C2 = Tantalum Capacitor [capacitance=10µF package="C 6032 [SMD, tantalum]"]
  R2 = Resistor [tolerance=±5% resistance=220 package="1206 [SMD]"]

nets:
  N1: J1.pin1, 1.Pin_1, LED1.cathode, C1.-, C2.-
  N2: J1.pin2, 1.Pin_4, 1.Pin_8, R2.Pin_0
  N3: 1.Pin_2, 1.Pin_6, C1.+, R1.Pin_0
  N4: 1.Pin_3, R3.Pin_0
  N5: 1.Pin_5, C2.+
  N6: 1.Pin_7, R1.Pin_1, R2.Pin_1
  N7: LED1.anode, R3.Pin_1

notes:
  HARVIE 555
